# Fritzing sketch kiln-controller (saved by Fritzing 0.9.2b)
breadboards: 1

parts:
  A1 = Arduino Uno (Rev3)
  D1 = 14-segment LED Alphanumeric Backpack [part_number=1911]

nets:
  N1: A1.A4/SDA, D1.SDA
  N2: A1.A5/SCL, D1.SCL
  GND: A1.GND, D1.GND
  3V3: A1.3V3, D1.VDD
  N3: A1.5V, D1.VI2C

custom parts:
  14-segment LED Alphanumeric Backpack: This is a nice, bright alphanumeric display that shows letters and numbers. It's super bright and designed for viewing from distances up to 23 feet (7 meters) away. Four digits with 14 segments on a black surface and we give you a set of two alphanumeric displays as well as a driver board so you can make a clock or a four letter word. Like our other LED backpacks, these are end-to-end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
